# Fritzing sketch capacitance_measure (saved by Fritzing 0.9.3b)
breadboards: 1

parts:
  U1 = atmega328 [package=dip]
  C1 = Ceramic Capacitor [capacitance=100nF package="200 mil [THT, multilayer]"]
  C2 = Electrolytic Capacitor [capacitance=1µF package="100 mil [THT, electrolytic]"]
  R1 = Resistor [tolerance=±5% resistance=1M package=THT]
  R2 = Resistor [tolerance=±5% resistance=100k package=THT]
  R3 = Resistor [tolerance=±5% resistance=10k package=THT]
  R4 = Resistor [tolerance=±5% resistance=1k package=THT]
  R5 = Resistor [tolerance=±5% resistance=100 package=THT]

nets:
  N1: U1.D2, R5.Pin_1
  N2: U1.D3_(PWM), R4.Pin_1
  N3: U1.XLAT2, R3.Pin_1
  N4: U1.D5_(PWM), R2.Pin_1
  N5: U1.D6_(PWM), R1.Pin_1
  N6: U1.D7, C2.+
  N7: U1.D9_(PWM), U1.GND#21, C1.0, C2.-, R1.Pin_0, R2.Pin_0, R3.Pin_0, R4.Pin_0, R5.Pin_0
  N8: U1.AVCC, C1.1
