# Fritzing sketch resistance_measure (saved by Fritzing 0.9.3b)
breadboards: 1

parts:
  U1 = atmega328 [package=dip]
  C1 = Electrolytic Capacitor [capacitance=0.1µF package="100 mil [THT, electrolytic]"]
  C = Ceramic Capacitor [capacitance=100nF package="100 mil [THT, multilayer]"]
  C2 = Electrolytic Capacitor [capacitance=1µF package="100 mil [THT, electrolytic]"]
  C3 = Electrolytic Capacitor [capacitance=10µF package="100 mil [THT, electrolytic]"]
  C5 = Electrolytic Capacitor [capacitance=0.1mF package="100 mil [THT, electrolytic]"]

nets:
  N1: U1.XLAT2, C5.+
  N2: U1.D5_(PWM), C3.+
  N3: U1.D6_(PWM), C2.+
  N4: U1.D7, C1.+
  N5: U1.D9_(PWM), U1.A0, C1.-, C2.-, C3.-, C5.-
  N6: U1.AVCC, C.1
  N7: U1.AREF, C.0
