# Fritzing sketch resistance_measure (saved by Fritzing 0.9.3b)
breadboards: 1

parts:
  U1 = atmega328 [package=dip]
  C1 = Capacitor [package=cap-pth-large]
  Rx = Resistor [tolerance=±5% resistance=220 package="2010 [SMD]"]

nets:
  N1: U1.A3, Rx.Pin_0
  N2: U1.A4, C1.2
  N3: U1.A5, C1.1, Rx.Pin_1
